# Fritzing sketch 1602lcd (saved by Fritzing 0.9.3b)
breadboards: 1

parts:
  LCD1 = LCD screen
  Mod1 = Raspberry Pi 4B
  R1 = Resistor [tolerance=±5% resistance=220 package="0402 [SMD]"]
  R2 = Rotary Potentiometer (Small) [maximum_resistance=100kΩ package=THT]

nets:
  VSS: LCD1.VSS, LCD1.R/W, LCD1.LED-, Mod1.GND, R2.leg2
  VDD: LCD1.VDD, Mod1.5V, R1.Pin_0, R2.leg1
  N1: LCD1.V0, R2.wiper
  N2: LCD1.RS, Mod1.GPIO25
  N3: LCD1.E, Mod1.GPIO24
  N4: LCD1.DB4, Mod1.GPIO23
  N5: LCD1.DB5, Mod1.GPIO17
  N6: LCD1.DB6, Mod1.GPIO18
  N7: LCD1.DB7, Mod1.GPIO22
  N8: LCD1.LED+, R1.Pin_1
