# Fritzing sketch 1chrelay (saved by Fritzing 0.9.3b)

parts:
  Mod1 = Raspberry Pi 4B
  Mod2 = KY-019 5V Relay Module [package="Breakout board"]
  BULB1 = Incandescent light bulb small [package="bulb sm"]
  JACK1 = 2.1mm Barrel Jack with Terminal Block

nets:
  N1: Mod1.5V, Mod2.+
  N2: Mod1.GPIO2, Mod2.S
  N3: Mod1.GND, Mod2.-
  N4: Mod2.Common, JACK1.NEG
  N5: Mod2.NO, BULB1.1
  N6: BULB1.2, JACK1.POS

custom parts:
  KY-019 5V Relay Module: KY-019 5V Relay module, used to control AC circuits. (Special thanks to vanepp for fixing the PCB holes and other errors)
