# Fritzing sketch 4x4keypad (saved by Fritzing 0.9.3b)
breadboards: 1

parts:
  Generic_4x4_button_keypad1 = Generic 4x4 Keypad
  Mod1 = Raspberry Pi 4B

nets:
  N1: Generic_4x4_button_keypad1.C4, Mod1.GPIO6
  N2: Generic_4x4_button_keypad1.C3, Mod1.GPIO7
  N3: Generic_4x4_button_keypad1.C2, Mod1.GPIO8
  N4: Generic_4x4_button_keypad1.C1, Mod1.GPIO9
  N5: Generic_4x4_button_keypad1.R1, Mod1.GPIO2
  N6: Generic_4x4_button_keypad1.R2, Mod1.GPIO3
  N7: Generic_4x4_button_keypad1.R3, Mod1.GPIO4
  N8: Generic_4x4_button_keypad1.R4, Mod1.GPIO5

custom parts:
  Generic 4x4 Keypad: generic 4x4 keypad 4 rows of four 6 mm tact switches cheap and nasty but works
