# Fritzing sketch 4x4keypad222 (saved by Fritzing 0.9.3b)
breadboards: 1

parts:
  Mod1 = Raspberry Pi 4B
  Generic_4x4_button_keypad1 = Generic 4x4 Keypad

nets:
  N1: Mod1.GPIO2, Generic_4x4_button_keypad1.R1
  N2: Mod1.GPIO3, Generic_4x4_button_keypad1.R2
  N3: Mod1.GPIO4, Generic_4x4_button_keypad1.R3
  N4: Mod1.GPIO9, Generic_4x4_button_keypad1.C1
  N5: Mod1.GPIO8, Generic_4x4_button_keypad1.C2
  N6: Mod1.GPIO7, Generic_4x4_button_keypad1.C3
  N7: Mod1.GPIO5, Generic_4x4_button_keypad1.R4
  N8: Mod1.GPIO6, Generic_4x4_button_keypad1.C4

custom parts:
  Generic 4x4 Keypad: generic 4x4 keypad 4 rows of four 6 mm tact switches cheap and nasty but works
