# Fritzing sketch adc+gas (saved by Fritzing 0.9.3b)
breadboards: 1

parts:
  Mod1 = Raspberry Pi 4B
  부품1 = Adafruit ADS1115 16Bit I2C ADC [part_number="Adafruit #1085"]
  Mod2 = MQ-7 breakout

nets:
  5V: Mod1.5V, 부품1.VDD, Mod2.VCC
  N1: Mod1.GPIO2, 부품1.SDA
  N2: Mod1.GPIO3, 부품1.SCL
  GND: Mod1.GND, 부품1.GND, Mod2.GND
  N3: Mod1.GPIO16, Mod2.DO
  N4: 부품1.AIN0, Mod2.AO

custom parts:
  Adafruit ADS1115 16Bit I2C ADC: For microcontrollers without an analog-to-digital converter or when you want a higher-precision ADC, the ADS1115 provides 16-bit precision at 860 samples/second over I2C. The chip can be configured as 4 single-ended input channels, or two differential channels. As a nice bonus, it even includes a programmable gain amplifier, up to x16, to help boost up smaller single/differential signals to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
  MQ-7 breakout: MQ-5 gas sensor
