# Fritzing sketch adc+sound (saved by Fritzing 0.9.3b)
breadboards: 1

parts:
  Mod1 = Raspberry Pi 4B
  부품1 = Adafruit ADS1115 16Bit I2C ADC [part_number="Adafruit #1085"]
  FC-1 = Sound Sensor

nets:
  5V: Mod1.5V, 부품1.VDD, FC-1.+
  N1: Mod1.GPIO2, 부품1.SDA
  N2: Mod1.GPIO3, 부품1.SCL
  GND: Mod1.GND, 부품1.GND, FC-1.G
  N3: Mod1.GPIO7, FC-1.DO
  N4: 부품1.AIN0, FC-1.AO

custom parts:
  Adafruit ADS1115 16Bit I2C ADC: For microcontrollers without an analog-to-digital converter or when you want a higher-precision ADC, the ADS1115 provides 16-bit precision at 860 samples/second over I2C. The chip can be configured as 4 single-ended input channels, or two differential channels. As a nice bonus, it even includes a programmable gain amplifier, up to x16, to help boost up smaller single/differential signals to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
  Sound Sensor: Sound Sensor with 4 pins
