# Fritzing sketch ir (saved by Fritzing 0.9.3b)
breadboards: 1

parts:
  Mod1 = Raspberry Pi 4B
  Mod2 = KY-022 Infrared Receiver Module [package="Breakout board"]

nets:
  N1: Mod1.3V3, Mod2.S
  N2: Mod1.GND, Mod2.-
  N3: Mod1.GPIO23, Mod2.Vin

custom parts:
  KY-022 Infrared Receiver Module: KY-022 IR receiver module, reacts to 38kHz infrared light.
