# Fritzing sketch pir (saved by Fritzing 0.9.3b)
breadboards: 1

parts:
  Mod1 = Raspberry Pi 4B
  PIR1 = PIR sensor
  LED1 = LED - 3mm [color="Red (633nm)" package="3 mm [THT]"]
  R1 = Resistor [tolerance=±5% resistance=220 package="0402 [SMD]"]

nets:
  5V: Mod1.5V, PIR1.VDD
  N1: Mod1.GPIO2, PIR1.SIG
  GND: Mod1.GND, PIR1.GND, R1.Pin_0
  N2: Mod1.GPIO13, LED1.anode
  N3: LED1.cathode, R1.Pin_1
