# Fritzing sketch rfid (saved by Fritzing 0.9.3b)
breadboards: 1

parts:
  Mod1 = Raspberry Pi 4B
  U1 = RFID RC522 SIP - 8 pins [chip_label="RFID RC522" package="SIP (Single Inline) [THT]"]

nets:
  3V3: Mod1.3V3, U1.VCC
  GND: Mod1.GND, U1.GND
  N1: Mod1.GPIO24, U1.MISO
  N2: Mod1.GPIO10, U1.SCK
  N3: Mod1.GPIO9, U1.MOSI
  N4: Mod1.GPIO25, U1.RST
  N5: Mod1.GPIO11, U1.NSS
  N6: Mod1.GPIO8, U1.IRQ

custom parts:
  RFID RC522 SIP - 8 pins: A SIP stand-in part for RFID RC522 . With 8 pins on a 300 mil single inline package (SIP) footprint.
