# Fritzing sketch segment (saved by Fritzing 0.9.3b)
breadboards: 1

parts:
  DI1 = 7-Segment LED Display [package=THT]
  R1 = Resistor [tolerance=±5% resistance=220 package="2010 [SMD]"]
  R2 = Resistor [tolerance=±5% resistance=220 package="2010 [SMD]"]
  R3 = Resistor [tolerance=±5% resistance=220 package="2010 [SMD]"]
  R4 = Resistor [tolerance=±5% resistance=220 package="2010 [SMD]"]
  R5 = Resistor [tolerance=±5% resistance=220 package="2010 [SMD]"]
  R6 = Resistor [tolerance=±5% resistance=220 package="2010 [SMD]"]
  R7 = Resistor [tolerance=±5% resistance=220 package="2010 [SMD]"]
  R8 = Resistor [tolerance=±5% resistance=220 package="2010 [SMD]"]
  Mod1 = Raspberry Pi 4B

nets:
  N1: DI1.cathodeE, R8.Pin_1
  N2: DI1.cathodeD, R7.Pin_1
  N3: DI1.commAnode, Mod1.5V
  N4: DI1.cathodeC, R5.Pin_0
  N5: DI1.cathodeDP, R6.Pin_0
  N6: DI1.cathodeB, R2.Pin_0
  N7: DI1.cathodeA, R1.Pin_0
  N8: DI1.cathodeF, R3.Pin_1
  N9: DI1.cathodeG, R4.Pin_1
  N10: R1.Pin_1, Mod1.GPIO2
  N11: R2.Pin_1, Mod1.GPIO3
  N12: R3.Pin_0, Mod1.GPIO8
  N13: R4.Pin_0, Mod1.GPIO7
  N14: R5.Pin_1, Mod1.GPIO4
  N15: R7.Pin_0, Mod1.GPIO5
  N16: R8.Pin_0, Mod1.GPIO6
