# Fritzing sketch shift_register (saved by Fritzing 0.9.3b)
breadboards: 1

parts:
  U1 = 74HC595 [package="DIP16 [THT]"]
  R1 = Resistor [tolerance=±5% resistance=220 package=THT]
  R2 = Resistor [tolerance=±5% resistance=220 package=THT]
  R3 = Resistor [tolerance=±5% resistance=220 package=THT]
  R4 = Resistor [tolerance=±5% resistance=220 package=THT]
  R5 = Resistor [tolerance=±5% resistance=220 package=THT]
  R6 = Resistor [tolerance=±5% resistance=220 package=THT]
  R7 = Resistor [tolerance=±5% resistance=220 package=THT]
  R8 = Resistor [tolerance=±5% resistance=220 package=THT]
  LED9 = LED - 3mm [color="Red (633nm)" package="3 mm [THT]"]
  LED10 = LED - 3mm [color="Red (633nm)" package="3 mm [THT]"]
  LED11 = LED - 3mm [color="Red (633nm)" package="3 mm [THT]"]
  LED12 = LED - 3mm [color="Red (633nm)" package="3 mm [THT]"]
  LED13 = LED - 3mm [color="Red (633nm)" package="3 mm [THT]"]
  LED14 = LED - 3mm [color="Red (633nm)" package="3 mm [THT]"]
  LED15 = LED - 3mm [color="Red (633nm)" package="3 mm [THT]"]
  LED16 = LED - 3mm [color="Red (633nm)" package="3 mm [THT]"]
  Mod1 = Raspberry Pi 4B

nets:
  N1: U1.Q1, R3.Pin_0
  N2: U1.Q2, R2.Pin_0
  N3: U1.Q3, R1.Pin_0
  N4: U1.Q4, R5.Pin_0
  N5: U1.Q5, R6.Pin_0
  N6: U1.Q6, R7.Pin_0
  N7: U1.Q7, R8.Pin_0
  GND: U1.GND, U1.OE, LED9.cathode, LED10.cathode, LED11.cathode, LED12.cathode, LED13.cathode, LED14.cathode, LED15.cathode, LED16.cathode, Mod1.GND
  VCC: U1.MR, U1.VCC, Mod1.5V
  N8: U1.SH_CP, Mod1.GPIO24
  N9: U1.ST_CP, Mod1.GPIO23
  N10: U1.DS, Mod1.GPIO22
  N11: U1.Q0, R4.Pin_0
  N12: R1.Pin_1, LED9.anode
  N13: R2.Pin_1, LED11.anode
  N14: R3.Pin_1, LED12.anode
  N15: R4.Pin_1, LED10.anode
  N16: R5.Pin_1, LED13.anode
  N17: R6.Pin_1, LED14.anode
  N18: R7.Pin_1, LED15.anode
  N19: R8.Pin_1, LED16.anode
