# Fritzing sketch stepmotor (saved by Fritzing 0.9.3b)

parts:
  Mod1 = Raspberry Pi 4B
  X1 = X113647 Stepper Driver Board [package=board]
  MOTOR1 = 28BYJ-48 Stepper Motor
  JACK1 = 2.1mm Barrel Jack with Terminal Block

nets:
  GND: Mod1.GND, X1.GND, JACK1.NEG
  N1: Mod1.GPIO12, X1.IN1
  N2: Mod1.GPIO16, X1.IN2
  N3: Mod1.GPIO20, X1.IN3
  N4: Mod1.GPIO21, X1.IN4
  N5: X1.+V, JACK1.POS
  N6: X1.BLUE, MOTOR1.BLUE
  N7: X1.PINK, MOTOR1.PINK
  N8: X1.YELLOW, MOTOR1.YELLOW
  N9: X1.ORANGE, MOTOR1.ORANGE
  N10: X1.RED, MOTOR1.RED

notes:
  POWER

custom parts:
  X113647 Stepper Driver Board: A common stepper motor driver board based on ULN2003APG darlington array
  28BYJ-48 Stepper Motor: 28BYJ-48 gear-reduction stepper motor (small)
