# Fritzing sketch tilt (saved by Fritzing 0.9.3b)
breadboards: 1

parts:
  Mod1 = Raspberry Pi 4B
  Tilt1 = SW520D [package=led10mm]
  R1 = Resistor [tolerance=±5% resistance=220 package="0603 [SMD]"]

nets:
  N1: Mod1.5V, R1.Pin_0
  N2: Mod1.GPIO24, Tilt1.Pin1, R1.Pin_1

custom parts:
  SW520D: Tilt Sensor
