# Fritzing sketch touchsensor (saved by Fritzing 0.9.3b)
breadboards: 1

parts:
  Mod1 = Raspberry Pi 4B
  TTP223B1 = TTP223B Capacitive Touch Sensor Module

nets:
  5V: Mod1.5V, TTP223B1.VCC
  GND: Mod1.GND, TTP223B1.GND
  N1: Mod1.GPIO24, TTP223B1.SIG

custom parts:
  TTP223B Capacitive Touch Sensor Module: The TTP223B capacitive touch sensor module uses the TTP223B IC. The appropriate voltage is approximately 2 to 5.5 volts.
